// Logisim project esq.circ as structural Verilog: 1 circuit, main circuit main
module main (
  input  A,
  input  B,
  input  C,
  input  D,
  output Q
);

  wire and_1_out, and_2_out, and_3_out, and_4_out, not_1_out, not_2_out, not_3_out, or_1_out, xor_1_out;

  not not_1 (not_1_out, C);
  xor xor_1 (xor_1_out, B, D);
  not not_2 (not_2_out, xor_1_out);
  and and_1 (and_1_out, B, D);
  and and_2 (and_2_out, not_2_out, not_1_out);
  and and_3 (and_3_out, and_1_out, A);
  not not_3 (not_3_out, and_3_out);
  or or_1 (or_1_out, and_2_out, and_4_out);
  and and_4 (and_4_out, C, not_3_out);
  or or_2 (Q, A, or_1_out);
endmodule
